# Fritzing sketch circuit (saved by Fritzing 0.9.2b)
breadboards: 1

parts:
  Part2 = Adafruit Feather 32u4 Bluefruit [part_number="Adafruit #2829"]
  R3 = Resistor [tolerance=±5% resistance=1M package=THT]
  U1 = CAPSENSE_PAD [package=capsense_pad]
  J1 = Basic Servo
  Flex_Sensor = Basic Flex Resistor [part_number="Adafruit #182"]
  R4 = Resistor [tolerance=±5% resistance=47k package=THT]

nets (from the schematic view):
  N1: Part2.A3, R3.Pin_1, U1.CONNECTOR
  N2: Part2.A2, R3.Pin_0
  N3: Part2.A1, Flex_Sensor.pin_1, R4.Pin_0
  N4: Part2.5, J1.pulse
  GND: J1.gnd, R4.Pin_1
  5V: J1.vcc, Flex_Sensor.Pin_2

notes:
  Leg Bag Emptier, Circuit for measuring and emptying leg bag, with back-up button., 1.0

custom parts:
  Adafruit Feather 32u4 Bluefruit: This is the Adafruit Feather 32u4 Bluefruit - our take on an 'all-in-one' Arduino-compatible + Bluetooth Low Energy with built in USB and battery charging. Its an Adafruit Feather 32u4 with a BTLE module, ready to rock! We have other boards in the Feather family, check'em out here. Bluetooth Low Energy is the hottest new low-power, 2.4GHz spectrum wireless protocol. In particular, its the only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
  CAPSENSE_PAD: Generic copper pad for a capacitive touch sensor.
